# Fritzing sketch StandandStare (saved by Fritzing 0.9.2b)
breadboards: 1

parts:
  RFID1 = RFID Reader
  Raspberry_Pi2 = Raspberry Pi B+
  R1 = Resistor [tolerance=±5% resistance=220 package=THT]
  LED2 = LED - 5mm [color="Red (633nm)" package="5 mm [THT]"]

nets:
  GND: RFID1.GND, RFID1.+/-, Raspberry_Pi2.GND, LED2.anode
  N1: RFID1.CP, Raspberry_Pi2.GPIO16, R1.Pin_0
  N2: RFID1.D0, Raspberry_Pi2.GPIO15
  +5V: RFID1.+5V, Raspberry_Pi2.3v3
  N3: R1.Pin_1, LED2.cathode
